// Logisim project ex2.circ as structural Verilog: 6 circuits, main circuit AND2
module AND2 (
  input  A,
  input  B,
  output RESULT
);

  and and_1 (RESULT, A, B);

  // Notes on the sheet:
  //   Sample Circuit
endmodule

module NAND2 (
  input  A,
  input  B,
  output RESULT
);
endmodule

module NOR2 (
  input  A,
  input  B,
  output RESULT
);
endmodule

module XOR2 (
  input  A,
  input  B,
  output RESULT
);
endmodule

module MUX2 (
  input  A,
  input  B,
  input  SEL,
  output RESULT
);
endmodule

module MUX4 (
  input  A,
  input  B,
  input  C,
  input  D,
  input  SEL0,
  input  SEL1,
  output RESULT
);
endmodule
